# Fritzing sketch ESQUEMA EN FRITZING (saved by Fritzing 0.6.3b)
breadboards: 1

parts:
  Arduino1 = Arduino
  LED1 = LED - 5mm [color="Red (633nm)" package="5 mm [THT]"]
  R1 = Resistor [tolerance=±5% resistance=220 package=THT]
  R2 = Resistor [tolerance=±5% resistance=220 package=THT]
  R3 = Resistor [tolerance=±5% resistance=220 package=THT]
  LCD1 = LCD screen
  J1 = Piezo Speaker
  R4 = Resistor [tolerance=±5% resistance=220 package=THT]
  R5 = Rotary Potentiometer (Small) [maximum_resistance=100kΩ]

nets:
  N1: Arduino1.D12, LCD1.RS
  N2: Arduino1.D11, LCD1.E
  N3: Arduino1.D9, J1.pin2
  N4: Arduino1.D8, LED1.anode
  N5: Arduino1.D5, LCD1.DB4
  N6: Arduino1.D4, LCD1.DB5
  N7: Arduino1.D3, LCD1.DB6
  N8: Arduino1.D2, LCD1.DB7
  N9: Arduino1.3V3, R3.Pin_0
  +5V: Arduino1.+5V, LCD1.VDD
  GND: Arduino1.GND, R2.Pin_1, LCD1.VSS, LCD1.R/W, R5.leg1
  N10: Arduino1.A4, R3.Pin_1
  N11: Arduino1.A5, R2.Pin_0
  N12: LED1.cathode, R1.Pin_0
  N13: LCD1.V0, R5.wiper
  N14: J1.pin1, R4.Pin_0
